# Fritzing sketch Ard-wifi_Bartender (saved by Fritzing 1.0.3b)
breadboards: 1

parts:
  HC-SR04_Sensor_1 = HC-SR04 Ultrasonic Distance Sensor
  M1 = DC Motor [voltage_(max)=6V voltage_(min)=3V]  # not connected
  M2 = DC Motor [voltage_(max)=6V voltage_(min)=3V]  # not connected
  M3 = DC Motor [voltage_(max)=6V voltage_(min)=3V]  # not connected
  M4 = DC Motor [voltage_(max)=6V voltage_(min)=3V]  # not connected
  M5 = DC Motor [voltage_(max)=6V voltage_(min)=3V]  # not connected
  M6 = DC Motor [voltage_(max)=6V voltage_(min)=3V]  # not connected
  M7 = DC Motor [voltage_(max)=6V voltage_(min)=3V]  # not connected
  M8 = DC Motor [voltage_(max)=6V voltage_(min)=3V]  # not connected
  M9 = DC Motor [voltage_(max)=6V voltage_(min)=3V]  # not connected
  M10 = DC Motor [voltage_(max)=6V voltage_(min)=3V]  # not connected
  M11 = DC Motor [voltage_(max)=6V voltage_(min)=3V]  # not connected
  M12 = DC Motor [voltage_(max)=6V voltage_(min)=3V]  # not connected
  A1 = Arduino UNO R4 WiFi
  U1 = 16-Channel Relay Module [package=relay-16ch]
  HX711_Weight_Sensor = Sparkfun load cell amplifier
  A2 = Hanmatek HM305
  J1 = Piezo Speaker
  A3 = yf-s401 flow sensor [package=THT]
  A4 = PFC8575 module
  OLED_I2C1 = OLED 128x64 I2C Monochrome Display

nets:
  N1: HC-SR04_Sensor_1.TRIG, A1.Pin_45
  N2: HC-SR04_Sensor_1.ECHO, A1.Pin_44
  GND: HC-SR04_Sensor_1.GND, A1.Pin_9, A1.Pin_30, A1.Pin_48, HX711_Weight_Sensor.Pin_6, J1.pin1, A3.pin2, OLED_I2C1.GND
  N3: A1.Pin_8, A1.Pin_27, U1.VCCOUT_5V, HX711_Weight_Sensor.Pin_9, HX711_Weight_Sensor.Pin_10, A3.pin1, OLED_I2C1.VDD
  N4: A1.Pin_40, OLED_I2C1.SDA
  N5: A1.Pin_41, OLED_I2C1.SCK
  N6: A1.Pin_42, HX711_Weight_Sensor.Pin_8
  N7: A1.Pin_43, HX711_Weight_Sensor.Pin_7
  N8: A1.Pin_47, A3.pin3
  N9: U1.VCC, A2.Pin_4
  N10: U1.GND, U1.OUT_GND, A2.Pin_3, A4.Pin_1, A4.Pin_20

custom parts:
  Arduino UNO R4 WiFi: The Arduino UNO R4 WiFi merges the RA4M1 microprocessor from Renesas with the ESP32-S3 from Espressif, creating an all-in-one tool for makers with enhanced processing power and a diverse array of new peripherals.
  16-Channel Relay Module: 16 channel relay module
  Sparkfun load cell amplifier: The SparkFun Load Cell Amplifier is a small breakout board for the HX711 IC that allows you to easily read load cells to measure weight.
  Hanmatek HM305: DC Power Supply 30V5A HM305.
  yf-s401 flow sensor: Flow sensors sit in line with your water line, and uses a pinwheel sensor to measure how much liquid has moved through it.
  PFC8575 module: PCF8575 IO Expander Module I2C To 16IO.

// code stored in the sketch: Ard-wifi_Bartender.ino
#include <Wire.h> // Include Wire library for I2C

// Devices
// 0. Webserver

// 1. EL-SM-008 LCD 
int lcd_sck = 7;
int lcd_sda = 6;

// 2. COM-07950 Passive Buzzer
int buzzer = 12;

// 3. HX711_Load_Cell
int load_clk = 9;
int load_dat = 8;

// 4. HC_SR04_UltraSonic Sensor
int sonic_trig = 11;
int sonic_echo = 10;

// 5. 16CH Relay (Using I2C relay board)
const int relay_address = 0x20; // Example I2C address for relay board

// 6. yf-s401-flow-sensor
int flow_pin = 13;    // This is the input pin on the Arduino
double flow_rate;     // This is the value we intend to calculate
volatile int flow_count; // This integer needs to be set as volatile to ensure it updates correctly during the interrupt process

void setup() {
  // Initialize I2C for LCD and Relay
  Wire.begin(); // Join I2C bus

  // Initialize the LCD
  pinMode(lcd_sck, OUTPUT);
  pinMode(lcd_sda, OUTPUT);

  // Initialize the buzzer
  pinMode(buzzer, OUTPUT);

  // Initialize the load cell
  pinMode(load_clk, OUTPUT);
  pinMode(load_dat, INPUT);

  // Initialize the ultrasonic sensor
  pinMode(sonic_trig, OUTPUT);
  pinMode(sonic_echo, INPUT);

  // Initialize the relays via I2C
  Wire.beginTransmission(relay_address);
  // Set up the relay board as needed
  Wire.endTransmission();

  // Initialize the flow sensor
  pinMode(flow_pin, INPUT);
  attachInterrupt(digitalPinToInterrupt(flow_pin), flowSensorISR, RISING); // Interrupt on rising edge
  flow_count = 0;

  // Begin Serial Communication for debugging
  Serial.begin(9600);
}

void loop() {
  // Add code to handle the devices
}

// Interrupt Service Routine for flow sensor
void flowSensorISR() {
  flow_count++;
}



/* 1. Standby
LCD: QR Barcode to connect
WEBSERVER: Waiting for connection
*/

/* 2. User Connected
WEBSERVER: Connect to %USER%
LCD: Show Connection to %USER%
BUZZER: Beep on connect
WEIGHT: check for change from default
ULTRASONIC:
RELAY:
PUMP[]:
FLOW:
*/

/* 3.Beverave List
WEBSERVER:
LCD:
BUZZER:
WEIGHT:
ULTRASONIC:
RELAY:
PUMP[]:
FLOW:
*/

/* 3.Pour Beverage
WEBSERVER:
LCD:
BUZZER:
WEIGHT:
ULTRASONIC:
RELAY:
PUMP[]:
FLOW:
*/

/* 3.Reset
WEBSERVER:
LCD:
BUZZER:
WEIGHT:
ULTRASONIC:
RELAY:
PUMP[]:
FLOW:
*/
